# Fritzing sketch Scheme (saved by Fritzing 0.9.3b)
breadboards: 1

parts:
  Part1 = Arduino Uno (Rev3)
  IC1 = DIP - 4 pins [chip_label="BiTronics EMG electrode" package="DIP (Dual Inline) [THT]"]
  IC2 = DIP - 8 pins [chip_label="BiTronics EMG" package="DIP (Dual Inline) [THT]"]
  IC3 = DIP - 4 pins [chip_label="BiTronics EMG electrode" package="DIP (Dual Inline) [THT]"]
  IC4 = DIP - 4 pins [chip_label="BiTronics EMG electrode" package="DIP (Dual Inline) [THT]"]
  LED1 = LED - 5mm [color="Green (570nm)" package="5 mm [THT]"]
  LED2 = LED - 5mm [color="Yellow (595nm)" package="5 mm [THT]"]
  R1 = Resistor [tolerance=±5% resistance=220 package=THT]
  R2 = Resistor [tolerance=±5% resistance=220 package=THT]
  IC5 = DIP - 8 pins [chip_label="BiTronics EMG" package="DIP (Dual Inline) [THT]"]
  IC6 = DIP - 4 pins [chip_label="BiTronics EMG electrode" package="DIP (Dual Inline) [THT]"]
  IC7 = DIP - 4 pins [chip_label="BiTronics EMG electrode" package="DIP (Dual Inline) [THT]"]
  IC8 = DIP - 4 pins [chip_label="BiTronics EMG electrode" package="DIP (Dual Inline) [THT]"]

nets:
  N1: Part1.D12/MISO, LED2.anode
  N2: Part1.D13/SCK, LED1.anode
  N3: Part1.GND, R1.Pin_0, R2.Pin_0
  N4: IC1.Elect, IC2.Elect_1
  N5: IC2.Elect_2, IC3.Elect
  N6: IC2.Ref, IC4.Elect
  N7: LED1.cathode, R1.Pin_1
  N8: LED2.cathode, R2.Pin_1
  N9: IC5.Elect_1, IC6.Elect
  N10: IC5.Elect_2, IC7.Elect
  N11: IC5.Ref, IC8.Elect

custom parts:
  DIP - 4 pins: A DIP stand-in part for whatever IC you want. With 4 pins on a 300mil dual inline package (DIP) footprint.
  DIP - 8 pins: A DIP stand-in part for whatever IC you want. With 8 pins on a 300mil dual inline package (DIP) footprint.
